// Logisim project alu.circ as structural Verilog: 1 circuit, main circuit alu
module alu (
  input  [31:0] A,
  input  [31:0] B,
  input  [3:0] ALUSel,
  output [31:0] ALUResult
);

  wire comparator_1_lt;
  wire [31:0] add0, AND0, MUL0, MULH0, MULHU0, OR0, sll0, slt0, SRA0, srl0, SUB0, XOR0;

  Multiplexer #(.select(4), .width(32)) multiplexer_1 (
    .in0(add0), .in1(sll0), .in2(slt0), .in4(XOR0), .in5(srl0), .in6(OR0), .in7(AND0), .in8(MUL0),
    .in9(MULH0), .in11(MULHU0), .in12(SUB0), .in13(SRA0), .in15(B), .out(ALUResult), .sel(ALUSel));  // open: in3, in10, in14
  Adder #(.width(32)) adder_1 (.a(A), .b(B), .out(add0));  // open: cin, cout
  Multiplexer #(.width(32)) multiplexer_2 (.in0({32{1'b0}}), .in1(32'h1), .out(slt0), .sel(comparator_1_lt));
  Comparator #(.width(32)) comparator_1 (.a(A), .b(B), .lt(comparator_1_lt));  // open: gt, eq
  Shifter #(.shift("lr"), .width(32)) shifter_1 (.in(A), .\dist (B[4:0]), .out(srl0));
  assign XOR0 = A ^ B;  // XOR_Gate xor_1, 32 bits wide
  assign OR0 = A | B;  // OR_Gate or_1, 32 bits wide
  assign AND0 = A & B;  // AND_Gate and_1, 32 bits wide
  Multiplier #(.mode("twosComplement"), .width(32)) multiplier_1 (.a(A), .b(B), .out(MUL0));  // open: cin, cout
  Multiplier #(.mode("twosComplement"), .width(32)) multiplier_2 (.a(A), .b(B), .cout(MULH0));  // open: out, cin
  Multiplier #(.width(32)) multiplier_3 (.a(A), .b(B), .cout(MULHU0));  // open: out, cin
  Subtractor #(.width(32)) subtractor_1 (.a(A), .b(B), .out(SUB0));  // open: bin, bout
  Shifter #(.shift("ar"), .width(32)) shifter_2 (.in(A), .\dist (B[4:0]), .out(SRA0));
  Shifter #(.width(32)) shifter_3 (.in(A), .\dist (B[4:0]), .out(sll0));

  // Other names for the same wires on the sheet: BSEL[31:0] = B

  // Notes on the sheet:
  //   INPUTS to your circuit
  //   DON'T CHANGE THE LOCATIONS OF THE INPUTS AND OUTPUTS!
  //   OUTPUT from your circuit
endmodule
