// Logisim project branch-comp.circ as structural Verilog: 1 circuit, main circuit branch_comp
module branch_comp (
  input  [31:0] BrData1,
  input  [31:0] BrData2,
  input  BrUn,
  output BrEq,
  output BrLt
);

  wire SignBrLt, UnBrLt;

  Comparator #(.width(32)) comparator_1 (.a(BrData1), .b(BrData2), .eq(BrEq));  // open: gt, lt
  Comparator #(.mode("unsigned"), .width(32)) comparator_2 (.a(BrData1), .b(BrData2), .lt(UnBrLt));  // open: gt, eq
  Multiplexer multiplexer_1 (.in0(SignBrLt), .in1(UnBrLt), .out(BrLt), .sel(BrUn));
  Comparator #(.width(32)) comparator_3 (.a(BrData1), .b(BrData2), .lt(SignBrLt));  // open: gt, eq

  // Notes on the sheet:
  //   INPUTS to your circuit
  //   DON'T CHANGE THE LOCATIONS OF THE INPUTS AND OUTPUTS!
  //   OUTPUT from your circuit
endmodule
