// Logisim project cpu.circ as structural Verilog: 1 circuit, main circuit cpu
module cpu (
  input  clk,
  input  [31:0] Instruction,
  input  [31:0] MemReadData,
  output [31:0] MemAddress,
  output [31:0] ProgramCounter,
  output [31:0] ra,
  output [31:0] sp,
  output [31:0] t0,
  output [31:0] t1,
  output [31:0] t2,
  output [31:0] s0,
  output [31:0] s1,
  output [31:0] a0,
  output [3:0] MemWriteMask,
  output [31:0] MemWriteData
);

  wire branch_comp_1_breq, branch_comp_1_brlt, control_logic_1_asel, control_logic_1_brun,
       control_logic_1_bsel, control_logic_1_memwen, control_logic_1_regwen, PCSel;
  wire [1:0] control_logic_1_wbsel;
  wire [2:0] control_logic_1_immsel;
  wire [3:0] control_logic_1_alusel;
  wire [31:0] adder_1_out, DataFromReg, imm_gen_1_immediate, InstructionS2, MemWB, multiplexer_1_out,
       multiplexer_2_out, multiplexer_3_out, multiplexer_4_out, ProgramCounterS2, regfile_1_readdata1,
       RegWriteData, UpdatedPC;

  Adder #(.width(32)) adder_1 (.a(ProgramCounter), .b(32'h4), .out(adder_1_out));  // open: cin, cout
  Multiplexer #(.width(32)) multiplexer_1 (.in0(Instruction), .in1({32{1'b0}}), .out(multiplexer_1_out), .sel(PCSel));
  Register #(.width(32)) PC (.D(multiplexer_2_out), .clk(clk), .Q(ProgramCounter));  // open: en, clr
  Multiplexer #(.width(32)) multiplexer_2 (.in0(adder_1_out), .in1(MemAddress), .out(multiplexer_2_out), .sel(PCSel));
  Register #(.width(32)) register_1 (.D(ProgramCounter), .clk(clk), .Q(ProgramCounterS2));  // open: en, clr
  Register #(.width(32)) INSTID (.D(multiplexer_1_out), .clk(clk), .Q(InstructionS2));  // open: en, clr
  control_logic control_logic_1 (
    .PCSel(PCSel), .RegWEn(control_logic_1_regwen), .ImmSel(control_logic_1_immsel),
    .BrUn(control_logic_1_brun), .ASel(control_logic_1_asel), .BSel(control_logic_1_bsel),
    .ALUSel(control_logic_1_alusel), .MemWEn(control_logic_1_memwen), .WBSel(control_logic_1_wbsel),
    .Instruction(InstructionS2), .BrEq(branch_comp_1_breq), .BrLt(branch_comp_1_brlt));
  regfile regfile_1 (
    .ReadIndex1(InstructionS2[19:15]), .ReadIndex2(InstructionS2[24:20]), .WriteIndex(InstructionS2[11:7]),
    .WriteData(RegWriteData), .RegWEn(control_logic_1_regwen), .clk(clk), .ra(ra), .sp(sp), .t0(t0), .t1(t1),
    .t2(t2), .s0(s0), .s1(s1), .a0(a0), .ReadData1(regfile_1_readdata1), .ReadData2(DataFromReg));
  imm_gen imm_gen_1 (.Instruction(InstructionS2), .ImmSel(control_logic_1_immsel), .Immediate(imm_gen_1_immediate));
  Multiplexer #(.width(32)) multiplexer_3 (
    .in0(DataFromReg), .in1(imm_gen_1_immediate), .out(multiplexer_3_out), .sel(control_logic_1_bsel));
  Adder #(.width(32)) adder_2 (.a(ProgramCounterS2), .b(32'h4), .out(UpdatedPC));  // open: cin, cout
  Multiplexer #(.width(32)) multiplexer_4 (
    .in0(regfile_1_readdata1), .in1(ProgramCounterS2), .out(multiplexer_4_out), .sel(control_logic_1_asel));
  alu alu_1 (.ALUResult(MemAddress), .A(multiplexer_4_out), .B(multiplexer_3_out), .ALUSel(control_logic_1_alusel));
  branch_comp branch_comp_1 (
    .BrData1(regfile_1_readdata1), .BrData2(DataFromReg), .BrUn(control_logic_1_brun),
    .BrEq(branch_comp_1_breq), .BrLt(branch_comp_1_brlt));
  Multiplexer #(.select(2), .width(32)) multiplexer_5 (
    .in0(UpdatedPC), .in1(MemAddress), .in2(MemWB), .out(RegWriteData), .sel(control_logic_1_wbsel));  // open: in3
  partial_store partial_store_1 (
    .Instruction(InstructionS2), .MemAddress(MemAddress), .DataFromReg(DataFromReg),
    .MemWEn(control_logic_1_memwen), .MemWriteMask(MemWriteMask), .DataToMem(MemWriteData));
  partial_load partial_load_1 (
    .Instruction(InstructionS2), .MemAddress(MemAddress), .DataFromMem(MemReadData), .DataToReg(MemWB));

  // Other names for the same wires on the sheet: InstructionS1[31:0] = Instruction;
  //   ProgramCounterS1[31:0] = ProgramCounter

  // Notes on the sheet:
  //   To IMEM
  //   IMEM (do **NOT** move this)
  //   From IMEM
  //   Inputs/Outputs for testing. Do **NOT** move these.
  //   It is OK to move the PC, RegFile, ALU, MEM, Branch Comp, Imm Gen, Partial Load, Partial Store and Control Logic to wherever is most convenient for you when constructing your CPU, and to delete this text
  //   To DMEM
  //   DMEM (do **NOT** move this)
  //   From DMEM
endmodule
