// Logisim project partial-load.circ as structural Verilog: 1 circuit, main circuit partial_load
module partial_load (
  input  [31:0] Instruction,
  input  [31:0] MemAddress,
  input  [31:0] DataFromMem,
  output [31:0] DataToReg
);

  wire comparator_2_eq, comparator_3_eq, comparator_4_eq, comparator_5_eq, comparator_6_eq, comparator_7_eq,
       comparator_8_eq, comparator_9_eq, comparator_10_eq, comparator_11_eq, comparator_12_eq,
       comparator_13_eq, comparator_14_eq, comparator_15_eq, comparator_16_eq, comparator_17_eq, is_I_type,
       is_lb_00, is_lb_01, is_lb_10, is_lb_11, is_lh_00, is_lh_01, is_lh_10, is_lw_00;
  wire [31:0] Extend0_7, Extend0_15, Extend8_15, Extend8_23, Extend16_23, Extend16_31, Extend24_31,
       multiplexer_1_out, multiplexer_2_out, multiplexer_3_out, multiplexer_4_out, multiplexer_5_out,
       multiplexer_6_out, multiplexer_7_out;

  assign Extend0_7 = {{24{DataFromMem[7]}}, DataFromMem[7:0]};  // Bit_Extender bit_extender_1
  assign Extend8_15 = {{24{DataFromMem[15]}}, DataFromMem[15:8]};  // Bit_Extender bit_extender_2
  assign Extend16_23 = {{24{DataFromMem[23]}}, DataFromMem[23:16]};  // Bit_Extender bit_extender_3
  assign Extend24_31 = {{24{DataFromMem[31]}}, DataFromMem[31:24]};  // Bit_Extender bit_extender_4
  assign Extend0_15 = {{16{DataFromMem[15]}}, DataFromMem[15:0]};  // Bit_Extender bit_extender_5
  assign Extend8_23 = {{16{DataFromMem[23]}}, DataFromMem[23:8]};  // Bit_Extender bit_extender_6
  assign Extend16_31 = {{16{DataFromMem[31]}}, DataFromMem[31:16]};  // Bit_Extender bit_extender_7
  Comparator #(.mode("unsigned"), .width(7)) comparator_1 (
    .a(7'b0000011), .b(Instruction[6:0]), .eq(is_I_type));  // open: gt, lt
  Comparator #(.width(3)) comparator_2 (.a(Instruction[14:12]), .b(3'b000), .eq(comparator_2_eq));  // open: gt, lt
  Comparator #(.mode("unsigned"), .width(2)) comparator_3 (
    .a(MemAddress[1:0]), .b(2'b00), .eq(comparator_3_eq));  // open: gt, lt
  Comparator #(.width(3)) comparator_4 (.a(Instruction[14:12]), .b(3'b000), .eq(comparator_4_eq));  // open: gt, lt
  Comparator #(.mode("unsigned"), .width(2)) comparator_5 (
    .a(MemAddress[1:0]), .b(2'b01), .eq(comparator_5_eq));  // open: gt, lt
  Comparator #(.width(3)) comparator_6 (.a(Instruction[14:12]), .b(3'b000), .eq(comparator_6_eq));  // open: gt, lt
  Comparator #(.mode("unsigned"), .width(2)) comparator_7 (
    .a(MemAddress[1:0]), .b(2'b10), .eq(comparator_7_eq));  // open: gt, lt
  Comparator #(.width(3)) comparator_8 (.a(Instruction[14:12]), .b(3'b000), .eq(comparator_8_eq));  // open: gt, lt
  Comparator #(.mode("unsigned"), .width(2)) comparator_9 (
    .a(MemAddress[1:0]), .b(2'b11), .eq(comparator_9_eq));  // open: gt, lt
  Comparator #(.width(3)) comparator_10 (.a(Instruction[14:12]), .b(3'b001), .eq(comparator_10_eq));  // open: gt, lt
  Comparator #(.mode("unsigned"), .width(2)) comparator_11 (
    .a(MemAddress[1:0]), .b(2'b00), .eq(comparator_11_eq));  // open: gt, lt
  Comparator #(.width(3)) comparator_12 (.a(Instruction[14:12]), .b(3'b001), .eq(comparator_12_eq));  // open: gt, lt
  Comparator #(.mode("unsigned"), .width(2)) comparator_13 (
    .a(MemAddress[1:0]), .b(2'b01), .eq(comparator_13_eq));  // open: gt, lt
  Comparator #(.width(3)) comparator_14 (.a(Instruction[14:12]), .b(3'b001), .eq(comparator_14_eq));  // open: gt, lt
  Comparator #(.mode("unsigned"), .width(2)) comparator_15 (
    .a(MemAddress[1:0]), .b(2'b10), .eq(comparator_15_eq));  // open: gt, lt
  Comparator #(.width(3)) comparator_16 (.a(Instruction[14:12]), .b(3'b010), .eq(comparator_16_eq));  // open: gt, lt
  Comparator #(.mode("unsigned"), .width(2)) comparator_17 (
    .a(MemAddress[1:0]), .b(2'b00), .eq(comparator_17_eq));  // open: gt, lt
  and and_1 (is_lb_00, is_I_type, comparator_2_eq, comparator_3_eq);
  and and_2 (is_lb_01, is_I_type, comparator_4_eq, comparator_5_eq);
  and and_3 (is_lb_10, is_I_type, comparator_6_eq, comparator_7_eq);
  and and_4 (is_lb_11, is_I_type, comparator_8_eq, comparator_9_eq);
  and and_5 (is_lh_00, is_I_type, comparator_10_eq, comparator_11_eq);
  and and_6 (is_lh_01, is_I_type, comparator_12_eq, comparator_13_eq);
  and and_7 (is_lh_10, is_I_type, comparator_14_eq, comparator_15_eq);
  and and_8 (is_lw_00, is_I_type, comparator_16_eq, comparator_17_eq);
  Multiplexer #(.width(32)) multiplexer_1 (.in0({32{1'b0}}), .in1(Extend0_7), .out(multiplexer_1_out), .sel(is_lb_00));
  Multiplexer #(.width(32)) multiplexer_2 (
    .in0(multiplexer_1_out), .in1(Extend8_15), .out(multiplexer_2_out), .sel(is_lb_01));
  Multiplexer #(.width(32)) multiplexer_3 (
    .in0(multiplexer_2_out), .in1(Extend16_23), .out(multiplexer_3_out), .sel(is_lb_10));
  Multiplexer #(.width(32)) multiplexer_4 (
    .in0(multiplexer_3_out), .in1(Extend24_31), .out(multiplexer_4_out), .sel(is_lb_11));
  Multiplexer #(.width(32)) multiplexer_5 (
    .in0(multiplexer_4_out), .in1(Extend0_15), .out(multiplexer_5_out), .sel(is_lh_00));
  Multiplexer #(.width(32)) multiplexer_6 (
    .in0(multiplexer_5_out), .in1(Extend8_23), .out(multiplexer_6_out), .sel(is_lh_01));
  Multiplexer #(.width(32)) multiplexer_7 (
    .in0(multiplexer_6_out), .in1(Extend16_31), .out(multiplexer_7_out), .sel(is_lh_10));
  Multiplexer #(.width(32)) multiplexer_8 (.in0(multiplexer_7_out), .in1(DataFromMem), .out(DataToReg), .sel(is_lw_00));

  // Other names for the same wires on the sheet: DFM0_7[7:0] = DataFromMem[7:0]; DFM0_15[15:0] = DataFromMem[15:0];
  //   DFM8_15[7:0] = DataFromMem[15:8]; DFM8_23[15:0] = DataFromMem[23:8]; DFM16_23[7:0] = DataFromMem[23:16];
  //   DFM16_31[15:0] = DataFromMem[31:16]; DFM24_31[7:0] = DataFromMem[31:24]; Funct3[2:0] = Instruction[14:12];
  //   MAddr00[1:0] = MemAddress[1:0]

  // Notes on the sheet:
  //   INPUTS to your circuit
  //   DON'T CHANGE THE LOCATIONS OF THE INPUTS AND OUTPUTS!
  //   OUTPUT from your circuit
endmodule
