// Logisim project partial-store.circ as structural Verilog: 1 circuit, main circuit partial_store
module partial_store (
  input  [31:0] Instruction,
  input  [31:0] MemAddress,
  input  [31:0] DataFromReg,
  input  MemWEn,
  output [3:0] MemWriteMask,
  output [31:0] DataToMem
);

  wire comparator_2_eq, comparator_3_eq, comparator_4_eq, comparator_5_eq, comparator_6_eq, comparator_7_eq,
       comparator_8_eq, comparator_9_eq, comparator_10_eq, comparator_11_eq, comparator_12_eq,
       comparator_13_eq, comparator_14_eq, comparator_15_eq, is_I_type, is_sb_00, is_sb_01, is_sb_10,
       is_sb_11, is_sh_00, is_sh_10, is_sw_00;
  wire [3:0] multiplexer_5_out, multiplexer_7_out, multiplexer_9_out, multiplexer_11_out, multiplexer_12_out,
       multiplexer_13_out;
  wire [31:0] multiplexer_1_out, multiplexer_2_out, multiplexer_3_out, multiplexer_4_out, multiplexer_6_out,
       multiplexer_8_out;

  Comparator #(.mode("unsigned"), .width(7)) comparator_1 (
    .a(7'b0100011), .b(Instruction[6:0]), .eq(is_I_type));  // open: gt, lt
  Comparator #(.width(3)) comparator_2 (.a(Instruction[14:12]), .b(3'b000), .eq(comparator_2_eq));  // open: gt, lt
  Comparator #(.mode("unsigned"), .width(2)) comparator_3 (
    .a(MemAddress[1:0]), .b(2'b00), .eq(comparator_3_eq));  // open: gt, lt
  Comparator #(.width(3)) comparator_4 (.a(Instruction[14:12]), .b(3'b000), .eq(comparator_4_eq));  // open: gt, lt
  Comparator #(.mode("unsigned"), .width(2)) comparator_5 (
    .a(MemAddress[1:0]), .b(2'b01), .eq(comparator_5_eq));  // open: gt, lt
  Comparator #(.width(3)) comparator_6 (.a(Instruction[14:12]), .b(3'b000), .eq(comparator_6_eq));  // open: gt, lt
  Comparator #(.mode("unsigned"), .width(2)) comparator_7 (
    .a(MemAddress[1:0]), .b(2'b10), .eq(comparator_7_eq));  // open: gt, lt
  Comparator #(.width(3)) comparator_8 (.a(Instruction[14:12]), .b(3'b000), .eq(comparator_8_eq));  // open: gt, lt
  Comparator #(.mode("unsigned"), .width(2)) comparator_9 (
    .a(MemAddress[1:0]), .b(2'b11), .eq(comparator_9_eq));  // open: gt, lt
  Comparator #(.width(3)) comparator_10 (.a(Instruction[14:12]), .b(3'b001), .eq(comparator_10_eq));  // open: gt, lt
  Comparator #(.mode("unsigned"), .width(2)) comparator_11 (
    .a(MemAddress[1:0]), .b(2'b00), .eq(comparator_11_eq));  // open: gt, lt
  Comparator #(.width(3)) comparator_12 (.a(Instruction[14:12]), .b(3'b001), .eq(comparator_12_eq));  // open: gt, lt
  Comparator #(.mode("unsigned"), .width(2)) comparator_13 (
    .a(MemAddress[1:0]), .b(2'b10), .eq(comparator_13_eq));  // open: gt, lt
  Comparator #(.width(3)) comparator_14 (.a(Instruction[14:12]), .b(3'b010), .eq(comparator_14_eq));  // open: gt, lt
  Comparator #(.mode("unsigned"), .width(2)) comparator_15 (
    .a(MemAddress[1:0]), .b(2'b00), .eq(comparator_15_eq));  // open: gt, lt
  and and_1 (is_sb_00, is_I_type, comparator_2_eq, comparator_3_eq);
  and and_2 (is_sb_01, is_I_type, comparator_4_eq, comparator_5_eq);
  and and_3 (is_sb_10, is_I_type, comparator_6_eq, comparator_7_eq);
  and and_4 (is_sb_11, is_I_type, comparator_8_eq, comparator_9_eq);
  and and_5 (is_sh_00, is_I_type, comparator_10_eq, comparator_11_eq);
  and and_6 (is_sh_10, is_I_type, comparator_12_eq, comparator_13_eq);
  and and_7 (is_sw_00, is_I_type, comparator_14_eq, comparator_15_eq);
  Multiplexer #(.width(32)) multiplexer_1 (
    .in0({32{1'b0}}), .in1({{24{1'b0}}, DataFromReg[7:0]}), .out(multiplexer_1_out), .sel(is_sb_00));
  Multiplexer #(.width(32)) multiplexer_2 (
    .in0(multiplexer_1_out), .in1({{16{1'b0}}, DataFromReg[7:0], {8{1'b0}}}), .out(multiplexer_2_out),
    .sel(is_sb_01));
  Multiplexer #(.width(32)) multiplexer_3 (
    .in0(multiplexer_2_out), .in1({{8{1'b0}}, DataFromReg[7:0], {16{1'b0}}}), .out(multiplexer_3_out),
    .sel(is_sb_10));
  Multiplexer #(.width(32)) multiplexer_4 (
    .in0(multiplexer_3_out), .in1({DataFromReg[7:0], {24{1'b0}}}), .out(multiplexer_4_out), .sel(is_sb_11));
  Multiplexer #(.width(4)) multiplexer_5 (.in0(4'b0000), .in1(4'b0001), .out(multiplexer_5_out), .sel(is_sb_00));
  Multiplexer #(.width(32)) multiplexer_6 (
    .in0(multiplexer_4_out), .in1({{16{1'b0}}, DataFromReg[15:0]}), .out(multiplexer_6_out), .sel(is_sh_00));
  Multiplexer #(.width(4)) multiplexer_7 (
    .in0(multiplexer_5_out), .in1(4'b0010), .out(multiplexer_7_out), .sel(is_sb_01));
  Multiplexer #(.width(32)) multiplexer_8 (
    .in0(multiplexer_6_out), .in1({DataFromReg[15:0], {16{1'b0}}}), .out(multiplexer_8_out), .sel(is_sh_10));
  Multiplexer #(.width(4)) multiplexer_9 (
    .in0(multiplexer_7_out), .in1(4'b0100), .out(multiplexer_9_out), .sel(is_sb_10));
  Multiplexer #(.width(32)) multiplexer_10 (
    .in0(multiplexer_8_out), .in1(DataFromReg), .out(DataToMem), .sel(is_sw_00));
  Multiplexer #(.width(4)) multiplexer_11 (
    .in0(multiplexer_9_out), .in1(4'b1000), .out(multiplexer_11_out), .sel(is_sb_11));
  Multiplexer #(.width(4)) multiplexer_12 (
    .in0(multiplexer_11_out), .in1(4'b0011), .out(multiplexer_12_out), .sel(is_sh_00));
  Multiplexer #(.width(4)) multiplexer_13 (
    .in0(multiplexer_12_out), .in1(4'b1100), .out(multiplexer_13_out), .sel(is_sh_10));
  Multiplexer #(.width(4)) multiplexer_14 (.in0(multiplexer_13_out), .in1(4'b1111), .out(MemWriteMask), .sel(is_sw_00));

  // Other names for the same wires on the sheet: DFG0_7[7:0] = DataFromReg[7:0]; DFG0_15[15:0] = DataFromReg[15:0];
  //   Extend_sb_00[7:0] = DataFromReg[7:0]; Extend_sb_01[15:8] = DataFromReg[7:0];
  //   Extend_sb_10[23:16] = DataFromReg[7:0]; Extend_sb_11[31:24] = DataFromReg[7:0];
  //   Extend_sh_00[15:0] = DataFromReg[15:0]; Extend_sh_10[31:16] = DataFromReg[15:0];
  //   Funct3[2:0] = Instruction[14:12]; MAddr00[1:0] = MemAddress[1:0]

  // Notes on the sheet:
  //   INPUTS to your circuit
  //   DON'T CHANGE THE LOCATIONS OF THE INPUTS AND OUTPUTS!
  //   OUTPUT from your circuit
endmodule
