// Logisim project regfile.circ as structural Verilog: 1 circuit, main circuit regfile
module regfile (
  input  [4:0] ReadIndex1,
  input  [4:0] ReadIndex2,
  input  [4:0] WriteIndex,
  input  [31:0] WriteData,
  input  RegWEn,
  input  clk,
  output [31:0] ra,
  output [31:0] sp,
  output [31:0] t0,
  output [31:0] t1,
  output [31:0] t2,
  output [31:0] s0,
  output [31:0] s1,
  output [31:0] a0,
  output [31:0] ReadData1,
  output [31:0] ReadData2
);

  wire RegWEn1, RegWEn2, RegWEn3, RegWEn4, RegWEn5, RegWEn6, RegWEn7, RegWEn8, RegWEn9, RegWEn10, RegWEn11,
       RegWEn12, RegWEn13, RegWEn14, RegWEn15, RegWEn16, RegWEn17, RegWEn18, RegWEn19, RegWEn20, RegWEn21,
       RegWEn22, RegWEn23, RegWEn24, RegWEn25, RegWEn26, RegWEn27, RegWEn28, RegWEn29, RegWEn30, RegWEn31,
       RegWEn32;
  wire [31:0] Reg1, Reg4, Reg5, Reg12, Reg13, Reg14, Reg15, Reg16, Reg17, Reg18, Reg19, Reg20, Reg21, Reg22,
       Reg23, Reg24, Reg25, Reg26, Reg27, Reg28, Reg29, Reg30, Reg31, Reg32;

  Register #(.width(32)) register_1 (.D(WriteData), .en(1'b0), .clk(clk), .Q(Reg1));  // open: clr
  Register #(.width(32)) register_2 (.D(WriteData), .en(RegWEn2), .clk(clk), .Q(ra));  // open: clr
  Register #(.width(32)) register_3 (.D(WriteData), .en(RegWEn4), .clk(clk), .Q(Reg4));  // open: clr
  Register #(.width(32)) register_4 (.D(WriteData), .en(RegWEn3), .clk(clk), .Q(sp));  // open: clr
  Register #(.width(32)) register_5 (.D(WriteData), .en(RegWEn5), .clk(clk), .Q(Reg5));  // open: clr
  Register #(.width(32)) register_6 (.D(WriteData), .en(RegWEn6), .clk(clk), .Q(t0));  // open: clr
  Register #(.width(32)) register_7 (.D(WriteData), .en(RegWEn7), .clk(clk), .Q(t1));  // open: clr
  Register #(.width(32)) register_8 (.D(WriteData), .en(RegWEn8), .clk(clk), .Q(t2));  // open: clr
  Register #(.width(32)) register_9 (.D(WriteData), .en(RegWEn9), .clk(clk), .Q(s0));  // open: clr
  Register #(.width(32)) register_10 (.D(WriteData), .en(RegWEn10), .clk(clk), .Q(s1));  // open: clr
  Register #(.width(32)) register_11 (.D(WriteData), .en(RegWEn11), .clk(clk), .Q(a0));  // open: clr
  Register #(.width(32)) register_12 (.D(WriteData), .en(RegWEn12), .clk(clk), .Q(Reg12));  // open: clr
  Register #(.width(32)) register_13 (.D(WriteData), .en(RegWEn13), .clk(clk), .Q(Reg13));  // open: clr
  Register #(.width(32)) register_14 (.D(WriteData), .en(RegWEn14), .clk(clk), .Q(Reg14));  // open: clr
  Register #(.width(32)) register_15 (.D(WriteData), .en(RegWEn15), .clk(clk), .Q(Reg15));  // open: clr
  Register #(.width(32)) register_16 (.D(WriteData), .en(RegWEn16), .clk(clk), .Q(Reg16));  // open: clr
  Register #(.width(32)) register_17 (.D(WriteData), .en(RegWEn17), .clk(clk), .Q(Reg17));  // open: clr
  Register #(.width(32)) register_18 (.D(WriteData), .en(RegWEn18), .clk(clk), .Q(Reg18));  // open: clr
  Register #(.width(32)) register_19 (.D(WriteData), .en(RegWEn19), .clk(clk), .Q(Reg19));  // open: clr
  Register #(.width(32)) register_20 (.D(WriteData), .en(RegWEn20), .clk(clk), .Q(Reg20));  // open: clr
  Register #(.width(32)) register_21 (.D(WriteData), .en(RegWEn21), .clk(clk), .Q(Reg21));  // open: clr
  Register #(.width(32)) register_22 (.D(WriteData), .en(RegWEn22), .clk(clk), .Q(Reg22));  // open: clr
  Register #(.width(32)) register_23 (.D(WriteData), .en(RegWEn23), .clk(clk), .Q(Reg23));  // open: clr
  Register #(.width(32)) register_24 (.D(WriteData), .en(RegWEn24), .clk(clk), .Q(Reg24));  // open: clr
  Register #(.width(32)) register_25 (.D(WriteData), .en(RegWEn25), .clk(clk), .Q(Reg25));  // open: clr
  Register #(.width(32)) register_26 (.D(WriteData), .en(RegWEn26), .clk(clk), .Q(Reg26));  // open: clr
  Register #(.width(32)) register_27 (.D(WriteData), .en(RegWEn27), .clk(clk), .Q(Reg27));  // open: clr
  Register #(.width(32)) register_28 (.D(WriteData), .en(RegWEn28), .clk(clk), .Q(Reg28));  // open: clr
  Register #(.width(32)) register_29 (.D(WriteData), .en(RegWEn29), .clk(clk), .Q(Reg29));  // open: clr
  Register #(.width(32)) register_30 (.D(WriteData), .en(RegWEn30), .clk(clk), .Q(Reg30));  // open: clr
  Register #(.width(32)) register_31 (.D(WriteData), .en(RegWEn31), .clk(clk), .Q(Reg31));  // open: clr
  Register #(.width(32)) register_32 (.D(WriteData), .en(RegWEn32), .clk(clk), .Q(Reg32));  // open: clr
  Demultiplexer #(.select(5)) demultiplexer_1 (
    .out0(RegWEn1), .out1(RegWEn2), .out2(RegWEn3), .out3(RegWEn4), .out4(RegWEn5), .out5(RegWEn6),
    .out6(RegWEn7), .out7(RegWEn8), .out8(RegWEn9), .out9(RegWEn10), .out10(RegWEn11), .out11(RegWEn12),
    .out12(RegWEn13), .out13(RegWEn14), .out14(RegWEn15), .out15(RegWEn16), .out16(RegWEn17),
    .out17(RegWEn18), .out18(RegWEn19), .out19(RegWEn20), .out20(RegWEn21), .out21(RegWEn22),
    .out22(RegWEn23), .out23(RegWEn24), .out24(RegWEn25), .out25(RegWEn26), .out26(RegWEn27),
    .out27(RegWEn28), .out28(RegWEn29), .out29(RegWEn30), .out30(RegWEn31), .out31(RegWEn32), .in(RegWEn),
    .sel(WriteIndex));
  Multiplexer #(.select(5), .width(32)) multiplexer_1 (
    .in0(Reg1), .in1(ra), .in2(sp), .in3(Reg4), .in4(Reg5), .in5(t0), .in6(t1), .in7(t2), .in8(s0), .in9(s1),
    .in10(a0), .in11(Reg12), .in12(Reg13), .in13(Reg14), .in14(Reg15), .in15(Reg16), .in16(Reg17),
    .in17(Reg18), .in18(Reg19), .in19(Reg20), .in20(Reg21), .in21(Reg22), .in22(Reg23), .in23(Reg24),
    .in24(Reg25), .in25(Reg26), .in26(Reg27), .in27(Reg28), .in28(Reg29), .in29(Reg30), .in30(Reg31),
    .in31(Reg32), .out(ReadData1), .sel(ReadIndex1));
  Multiplexer #(.select(5), .width(32)) multiplexer_2 (
    .in0(Reg1), .in1(ra), .in2(sp), .in3(Reg4), .in4(Reg5), .in5(t0), .in6(t1), .in7(t2), .in8(s0), .in9(s1),
    .in10(a0), .in11(Reg12), .in12(Reg13), .in13(Reg14), .in14(Reg15), .in15(Reg16), .in16(Reg17),
    .in17(Reg18), .in18(Reg19), .in19(Reg20), .in20(Reg21), .in21(Reg22), .in22(Reg23), .in23(Reg24),
    .in24(Reg25), .in25(Reg26), .in26(Reg27), .in27(Reg28), .in28(Reg29), .in29(Reg30), .in30(Reg31),
    .in31(Reg32), .out(ReadData2), .sel(ReadIndex2));

  // Notes on the sheet:
  //   INPUTS to your circuit
  //   DON'T CHANGE THE LOCATIONS OF THE INPUTS AND OUTPUTS!
  //   These are DEBUG/TEST outputs from your circuit.
  //   OUTPUTS from your circuit
endmodule
